// Logisim project S-MIPS.circ as structural Verilog: 6 circuits, main circuit Register File
module Register_File (
  input  [31:0] DI,
  input  R_W,
  input  [4:0] Rd,
  input  [4:0] Rs,
  input  [4:0] Rt,
  input  Clk,
  input  Reset,
  input  in_8,
  input  in_9,
  output [31:0] DRs,
  output [31:0] DRt,
  output [31:0] Hi_Lo
);

  wire L0, L1, L2, L3, L4, L5, L6, L7, L8, L9, L10, L11, L12, L13, L14, L15, L16, L17, L18, L19, L20, L21,
       L22, L23, L24, L25, L26, L27, L28, L29, L30, LSP;
  wire [31:0] H, Hi, L, Lo, Q0, Q1, Q2, Q3, Q4, Q5, Q6, Q7, Q8, Q9, Q10, Q11, Q12, Q13, Q14, Q15, Q16, Q17,
       Q18, Q19, Q20, Q21, Q22, Q23, Q24, Q25, Q26, Q27, Q28, Q29, Q30, QSP;

  Register #(.width(32)) R0 (.Q(Q0), .clk(Clk), .clr(Reset));  // open: D, en
  Register #(.width(32)) R6 (.D(DI), .en(L6), .Q(Q6), .clk(Clk), .clr(Reset));
  Register #(.width(32)) R12 (.D(DI), .en(L12), .Q(Q12), .clk(Clk), .clr(Reset));
  Register #(.width(32)) R18 (.D(DI), .en(L18), .Q(Q18), .clk(Clk), .clr(Reset));
  Register #(.width(32)) R24 (.D(DI), .en(L24), .Q(Q24), .clk(Clk), .clr(Reset));
  Register #(.width(32)) R30 (.D(DI), .en(L30), .Q(Q30), .clk(Clk), .clr(Reset));
  Register #(.width(32)) R1 (.D(DI), .en(L1), .Q(Q1), .clk(Clk), .clr(Reset));
  Register #(.width(32)) R7 (.D(DI), .en(L7), .Q(Q7), .clk(Clk), .clr(Reset));
  Register #(.width(32)) R13 (.D(DI), .en(L13), .Q(Q13), .clk(Clk), .clr(Reset));
  Register #(.width(32)) R19 (.D(DI), .en(L19), .Q(Q19), .clk(Clk), .clr(Reset));
  Register #(.width(32)) R25 (.D(DI), .en(L25), .Q(Q25), .clk(Clk), .clr(Reset));
  Register #(.width(32)) SP ();  // open: D, en, Q, clk, clr
  Register #(.width(32)) R2 (.D(DI), .en(L2), .Q(Q2), .clk(Clk), .clr(Reset));
  Register #(.width(32)) R8 (.D(DI), .en(L8), .Q(Q8), .clk(Clk), .clr(Reset));
  Register #(.width(32)) R14 (.D(DI), .en(L14), .Q(Q14), .clk(Clk), .clr(Reset));
  Register #(.width(32)) R20 (.D(DI), .en(L20), .Q(Q20), .clk(Clk), .clr(Reset));
  Register #(.width(32)) R26 (.D(DI), .en(L26), .Q(Q26), .clk(Clk), .clr(Reset));
  Register #(.width(32)) u_Lo (.D(L), .en(in_8), .Q(Lo), .clk(Clk), .clr(Reset));
  Register #(.width(32)) R3 (.D(DI), .en(L3), .Q(Q3), .clk(Clk), .clr(Reset));
  Register #(.width(32)) R9 (.D(DI), .en(L9), .Q(Q9), .clk(Clk), .clr(Reset));
  Register #(.width(32)) R15 (.D(DI), .en(L15), .Q(Q15), .clk(Clk), .clr(Reset));
  Register #(.width(32)) R21 (.D(DI), .en(L21), .Q(Q21), .clk(Clk), .clr(Reset));
  Register #(.width(32)) R27 (.D(DI), .en(L27), .Q(Q27), .clk(Clk), .clr(Reset));
  Register #(.width(32)) u_Hi (.D(H), .en(in_8), .Q(Hi), .clk(Clk), .clr(Reset));
  Register #(.width(32)) R4 (.D(DI), .en(L4), .Q(Q4), .clk(Clk), .clr(Reset));
  Register #(.width(32)) R10 (.D(DI), .en(L10), .Q(Q10), .clk(Clk), .clr(Reset));
  Register #(.width(32)) R16 (.D(DI), .en(L16), .Q(Q16), .clk(Clk), .clr(Reset));
  Register #(.width(32)) R22 (.D(DI), .en(L22), .Q(Q22), .clk(Clk), .clr(Reset));
  Register #(.width(32)) R28 (.D(DI), .en(L28), .Q(Q28), .clk(Clk), .clr(Reset));
  Register #(.width(32)) R5 (.D(DI), .en(L5), .Q(Q5), .clk(Clk), .clr(Reset));
  Register #(.width(32)) R11 (.D(DI), .en(L11), .Q(Q11), .clk(Clk), .clr(Reset));
  Register #(.width(32)) R17 (.D(DI), .en(L17), .Q(Q17), .clk(Clk), .clr(Reset));
  Register #(.width(32)) R23 (.D(DI), .en(L23), .Q(Q23), .clk(Clk), .clr(Reset));
  Register #(.width(32)) R29 (.D(DI), .en(L29), .Q(Q29), .clk(Clk), .clr(Reset));
  Demultiplexer #(.select(5)) demultiplexer_1 (
    .out0(L0), .out1(L1), .out2(L2), .out3(L3), .out4(L4), .out5(L5), .out6(L6), .out7(L7), .out8(L8),
    .out9(L9), .out10(L10), .out11(L11), .out12(L12), .out13(L13), .out14(L14), .out15(L15), .out16(L16),
    .out17(L17), .out18(L18), .out19(L19), .out20(L20), .out21(L21), .out22(L22), .out23(L23), .out24(L24),
    .out25(L25), .out26(L26), .out27(L27), .out28(L28), .out29(L29), .out30(L30), .out31(LSP), .in(R_W),
    .sel(Rd));  // open: en
  Multiplexer #(.select(5), .width(32)) multiplexer_1 (
    .in0(Q0), .in1(Q1), .in2(Q2), .in3(Q3), .in4(Q4), .in5(Q5), .in6(Q6), .in7(Q7), .in8(Q8), .in9(Q9),
    .in10(Q10), .in11(Q11), .in12(Q12), .in13(Q13), .in14(Q14), .in15(Q15), .in16(Q16), .in17(Q17),
    .in18(Q18), .in19(Q19), .in20(Q20), .in21(Q21), .in22(Q22), .in23(Q23), .in24(Q24), .in25(Q25),
    .in26(Q26), .in27(Q27), .in28(Q28), .in29(Q29), .in30(Q30), .in31(QSP), .out(DRs), .sel(Rs));  // open: en
  Multiplexer #(.select(5), .width(32)) multiplexer_2 (
    .in0(Q0), .in1(Q1), .in2(Q2), .in3(Q3), .in4(Q4), .in5(Q5), .in6(Q6), .in7(Q7), .in8(Q8), .in9(Q9),
    .in10(Q10), .in11(Q11), .in12(Q12), .in13(Q13), .in14(Q14), .in15(Q15), .in16(Q16), .in17(Q17),
    .in18(Q18), .in19(Q19), .in20(Q20), .in21(Q21), .in22(Q22), .in23(Q23), .in24(Q24), .in25(Q25),
    .in26(Q26), .in27(Q27), .in28(Q28), .in29(Q29), .in30(Q30), .in31(QSP), .out(DRt), .sel(Rt));  // open: en
  Multiplexer #(.width(32), .enable("false")) multiplexer_3 (.in0(Hi), .in1(Lo), .out(Hi_Lo), .sel(in_9));

  // Other names for the same wires on the sheet: LM_D = in_8; Rst = Reset; Selector_H_L = in_9

  // Notes on the sheet:
  //   Inputs
  //   Data in
  //   Read/Write
  //   Data Address
  //   Selector A
  //   Selector B
  //   Clock
  //   Reset
  //   Register File
  //   Outputs
  //   Data out
  //   Data out
  //   Data out
endmodule

module ALU (
  input  [31:0] A,
  input  [31:0] B,
  input  [3:0] Operation,
  output [31:0] out,
  output ZF,
  output NF,
  output [31:0] Hi
);

  wire comparator_1_lt, comparator_2_lt, nor_2_out;
  wire [31:0] add, \and , hi_div, hi_divu, hi_mul, hi_mulu, lo_div, lo_divu, lo_mul, lo_mulu, \nor , \or ,
       S_less, sub, U_less, \xor ;

  Multiplier #(.width(32)) multiplier_1 (.a(A), .b(B), .out(lo_mul), .cout(hi_mul));  // open: cin
  Mulu mulu_1 (.A(A), .B(B), .Lo(lo_mulu), .Hi(hi_mulu));
  Div div_1 (.A(A), .B(B), .Lo(lo_div), .Hi(hi_div));
  Comparator #(.width(32)) comparator_1 (.a(A), .b(B), .lt(comparator_1_lt));  // open: gt, eq
  assign S_less = {{31{1'b0}}, comparator_1_lt};  // Bit_Extender bit_extender_1
  Adder #(.width(32)) adder_1 (.a(A), .b(B), .out(add));  // open: cin, cout
  Subtractor #(.width(32)) subtractor_1 (.a(A), .b(B), .out(sub));  // open: bin, bout
  Divider #(.width(32)) divider_1 (.a(A), .b(B), .out(lo_divu), .rem(hi_divu));  // open: upper
  assign \and  = A & B;  // AND_Gate and_1, 32 bits wide
  assign \or  = A | B;  // OR_Gate or_1, 32 bits wide
  Comparator #(.width(32), .mode("unsigned")) comparator_2 (.a(A), .b(B), .lt(comparator_2_lt));  // open: gt, eq
  assign U_less = {{31{1'b0}}, comparator_2_lt};  // Bit_Extender bit_extender_2
  assign \nor  = ~(A | B);  // NOR_Gate nor_1, 32 bits wide
  assign \xor  = A ^ B;  // XOR_Gate xor_1, 32 bits wide
  Multiplexer #(.select(4), .width(32), .enable("false")) multiplexer_1 (
    .in0(lo_mul), .in1(lo_mulu), .in2(lo_div), .in3(lo_divu), .in4(add), .in5(sub), .in6(\and ), .in7(\or ),
    .in8(\nor ), .in9(\xor ), .in10(S_less), .in11(U_less), .out(out), .sel(Operation));  // open: in12, in13, in14, in15
  Multiplexer #(.select(2), .width(32)) multiplexer_2 (
    .in0(hi_mul), .in1(hi_mulu), .in2(hi_div), .in3(hi_divu), .out(Hi), .sel(Operation[1:0]), .en(nor_2_out));
  nor nor_2 (nor_2_out, Operation[2], Operation[3]);
  Comparator #(.width(32)) comparator_3 (.a(out), .b({32{1'b0}}), .eq(ZF), .lt(NF));  // open: gt

  // Other names for the same wires on the sheet: Op[3:0] = Operation

  // Notes on the sheet:
  //   Inputs
  //   Aritmetic Logic Unit
  //   Outputs
endmodule

module Data_Path (
  input  [31:0] in_1,
  input  in_2,
  input  in_3,
  input  in_4,
  input  in_5,
  output [15:0] out_6,
  output [31:0] out_7,
  output [31:0] out_8,
  output out_9,
  output out_10,
  output out_11,
  output out_12
);

  wire M, N, R_W, S_H_L, SDATA, SData_t, Z;
  wire [3:0] Op;
  wire [4:0] DataAddress, Selector_A, Selector_B;
  wire [31:0] B, carry, Data_In, Hi_Lo, multiplexer_1_out, multiplexer_3_out, out, PC, PC_jump;

  Register #(.width(32)) Program_Counter (.D(PC_jump), .en(in_5), .Q(PC), .clk(in_3), .clr(in_2));
  // Register_File register_file_1: pin names not known; wires that end beside it: Data_In, R_W, DataAddress, Selector_A, Selector_B, in_3, S_H_L, in_2, out_7, B, Hi_Lo
  Multiplexer #(.width(32), .enable("false")) multiplexer_1 (
    .in0(out_7), .in1(B), .out(multiplexer_1_out), .sel(SData_t));
  Multiplexer #(.width(32), .enable("false")) multiplexer_2 (.in0(B), .in1(out_7), .out(out_8), .sel(SDATA));
  Multiplexer #(.width(32), .enable("false")) multiplexer_3 (
    .in0(multiplexer_1_out), .in1(Hi_Lo), .out(multiplexer_3_out), .sel(M));
  ALU alu_1 (.A(multiplexer_3_out), .Operation(Op), .out(out), .ZF(Z), .NF(N), .Hi(carry));  // open: B

  // Other names for the same wires on the sheet: A[31:0] = out_7; address[15:0] = out_6; Clk = in_3; End = out_9;
  //   Input[31:0] = in_1; Load = out_10; Memory_Data[31:0] = out_8; PC_Enable = in_5; Push = out_11; RAM_R_W = out_12;
  //   Reset = in_2; RW = in_4

  // Notes on the sheet:
  //   Inputs
  //   Data Path
  //   Outputs
endmodule

module Cache_Memory (
  input  [31:0] in_1,
  input  [31:0] Luego_te_nombro,
  input  in_3,
  input  in_4,
  input  in_5,
  output [15:0] out_6,
  output [31:0] out_7
);

  wire en0, en1, en2, en3, en4, en5, en6, en7, Hit, V0, V1, V2, V3, V4, V5, V6, V7, Validate, Value_Ram;
  wire [2:0] Index_Ram, luego_te_nombro_t, multiplexer_1_out;
  wire [12:0] T0, T1, T2, T3, T4, T5, T6, T7, tag;
  wire [31:0] IN1, IN2, IN3, O0, O1, O2, O3, O4, O5, O6, O7, O8, O9, O10, O11, O12, O13, O14, O15, O16, O17,
       O18, O19, O20, O21, O22, O23, O24, O25, O26, O27, O28, O29, O30, O31;

  Register #(.width(13)) register_1 (.D(tag), .en(en0), .Q(T0), .clk(in_3), .clr(in_4));
  Register #(.width(13)) register_2 (.D(tag), .en(en1), .Q(T1), .clk(in_3), .clr(in_4));
  Register #(.width(13)) register_3 (.D(tag), .en(en2), .Q(T2), .clk(in_3), .clr(in_4));
  Register #(.width(13)) register_4 (.D(tag), .en(en3), .Q(T3), .clk(in_3), .clr(in_4));
  Register #(.width(13)) register_5 (.D(tag), .en(en4), .Q(T4), .clk(in_3), .clr(in_4));
  Register #(.width(13)) register_6 (.D(tag), .en(en5), .Q(T5), .clk(in_3), .clr(in_4));
  Register #(.width(13)) register_7 (.D(tag), .en(en6), .Q(T6), .clk(in_3), .clr(in_4));
  Register #(.width(13)) register_8 (.D(tag), .en(en7), .Q(T7), .clk(in_3), .clr(in_4));
  Register #(.width(32)) register_9 (.D(in_1), .en(en0), .Q(O0), .clk(in_3), .clr(in_4));
  Register #(.width(32)) register_10 (.D(in_1), .en(en1), .Q(O4), .clk(in_3), .clr(in_4));
  Register #(.width(32)) register_11 (.D(in_1), .en(en2), .Q(O8), .clk(in_3), .clr(in_4));
  Register #(.width(32)) register_12 (.D(in_1), .en(en3), .Q(O12), .clk(in_3), .clr(in_4));
  Register #(.width(32)) register_13 (.D(in_1), .en(en4), .Q(O16), .clk(in_3), .clr(in_4));
  Register #(.width(32)) register_14 (.D(in_1), .en(en5), .Q(O20), .clk(in_3), .clr(in_4));
  Register #(.width(32)) register_15 (.D(in_1), .en(en6), .Q(O24), .clk(in_3), .clr(in_4));
  Register #(.width(32)) register_16 (.D(in_1), .en(en7), .Q(O28), .clk(in_3), .clr(in_4));
  Register #(.width(32)) register_17 (.D(IN1), .en(en0), .Q(O1), .clk(in_3), .clr(in_4));
  Register #(.width(32)) register_18 (.D(IN1), .en(en1), .Q(O5), .clk(in_3), .clr(in_4));
  Register #(.width(32)) register_19 (.D(IN1), .en(en2), .Q(O9), .clk(in_3), .clr(in_4));
  Register #(.width(32)) register_20 (.D(IN1), .en(en3), .Q(O13), .clk(in_3), .clr(in_4));
  Register #(.width(32)) register_21 (.D(IN1), .en(en4), .Q(O17), .clk(in_3), .clr(in_4));
  Register #(.width(32)) register_22 (.D(IN1), .en(en5), .Q(O21), .clk(in_3), .clr(in_4));
  Register #(.width(32)) register_23 (.D(IN1), .en(en6), .Q(O25), .clk(in_3), .clr(in_4));
  Register #(.width(32)) register_24 (.D(IN1), .en(en7), .Q(O29), .clk(in_3), .clr(in_4));
  Register #(.width(32)) register_25 (.D(IN2), .en(en0), .Q(O2), .clk(in_3), .clr(in_4));
  Register #(.width(32)) register_26 (.D(IN2), .en(en1), .Q(O6), .clk(in_3), .clr(in_4));
  Register #(.width(32)) register_27 (.D(IN2), .en(en2), .Q(O10), .clk(in_3), .clr(in_4));
  Register #(.width(32)) register_28 (.D(IN2), .en(en3), .Q(O14), .clk(in_3), .clr(in_4));
  Register #(.width(32)) register_29 (.D(IN2), .en(en4), .Q(O18), .clk(in_3), .clr(in_4));
  Register #(.width(32)) register_30 (.D(IN2), .en(en5), .Q(O22), .clk(in_3), .clr(in_4));
  Register #(.width(32)) register_31 (.D(IN2), .en(en6), .Q(O26), .clk(in_3), .clr(in_4));
  Register #(.width(32)) register_32 (.D(IN2), .en(en7), .Q(O30), .clk(in_3), .clr(in_4));
  Register #(.width(32)) register_33 (.D(IN3), .en(en0), .Q(O3), .clk(in_3), .clr(in_4));
  Register #(.width(32)) register_34 (.D(IN3), .en(en1), .Q(O7), .clk(in_3), .clr(in_4));
  Register #(.width(32)) register_35 (.D(IN3), .en(en2), .Q(O11), .clk(in_3), .clr(in_4));
  Register #(.width(32)) register_36 (.D(IN3), .en(en3), .Q(O15), .clk(in_3), .clr(in_4));
  Register #(.width(32)) register_37 (.D(IN3), .en(en4), .Q(O19), .clk(in_3), .clr(in_4));
  Register #(.width(32)) register_38 (.D(IN3), .en(en5), .Q(O23), .clk(in_3), .clr(in_4));
  Register #(.width(32)) register_39 (.D(IN3), .en(en6), .Q(O27), .clk(in_3), .clr(in_4));
  Register #(.width(32)) register_40 (.D(IN3), .en(en7), .Q(O31), .clk(in_3), .clr(in_4));
  D_Flip_Flop d_ff_1 (.clk(in_3), .D(Validate), .Q(V0), .en(en0), .reset(in_4));  // open: Qn, preset
  D_Flip_Flop d_ff_2 (.clk(in_3), .D(Validate), .Q(V1), .en(en1), .reset(in_4));  // open: Qn, preset
  D_Flip_Flop d_ff_3 (.clk(in_3), .D(Validate), .Q(V2), .en(en2), .reset(in_4));  // open: Qn, preset
  D_Flip_Flop d_ff_4 (.clk(in_3), .D(Validate), .Q(V3), .en(en3), .reset(in_4));  // open: Qn, preset
  D_Flip_Flop d_ff_5 (.clk(in_3), .D(Validate), .Q(V4), .en(en4), .reset(in_4));  // open: Qn, preset
  D_Flip_Flop d_ff_6 (.clk(in_3), .D(Validate), .Q(V5), .en(en5), .reset(in_4));  // open: Qn, preset
  D_Flip_Flop d_ff_7 (.clk(in_3), .D(Validate), .Q(V6), .en(en6), .reset(in_4));  // open: Qn, preset
  D_Flip_Flop d_ff_8 (.clk(in_3), .D(Validate), .Q(V7), .en(en7), .reset(in_4));  // open: Qn, preset
  Demultiplexer #(.select(3), .enable("false")) demultiplexer_1 (
    .out0(en0), .out1(en1), .out2(en2), .out3(en3), .out4(en4), .out5(en5), .out6(en6), .out7(en7), .in(Hit),
    .sel(multiplexer_1_out));
  Multiplexer #(.width(3), .enable("false")) multiplexer_1 (
    .in0(luego_te_nombro_t), .in1(Index_Ram), .out(multiplexer_1_out), .sel(in_5));
  Multiplexer #(.select(3), .enable("false")) multiplexer_2 (
    .in0(V0), .in1(V1), .in2(V2), .in3(V3), .in4(V4), .in5(V5), .in6(V6), .in7(V7), .out(Value_Ram),
    .sel(Index_Ram));

  // Other names for the same wires on the sheet: Address_Ram[15:0] = out_6; Clk = in_3; IN0[31:0] = in_1;
  //   Out[31:0] = out_7; R_W = in_5; Reset = in_4

  // Notes on the sheet:
  //   in_1: pull=down
  //   Luego_te_nombro: pull=down
  //   Inputs
  //   Tag
  //   Cache Memory
  //   Cache
  //   _____________________________________________________________________________
  //   _____________________________________________________________________________
  //   _____________________________________________________________________________
  //   _____________________________________________________________________________
  //   _____________________________________________________________________________
  //   _____________________________________________________________________________
  //   _____________________________________________________________________________
  //   Validate
  //   Outputs
endmodule

module Mulu (
  input  [31:0] A,
  input  [31:0] B,
  output [31:0] Lo,
  output [31:0] Hi
);

  wire [31:0] adder_1_out, multiplexer_1_out, multiplexer_2_out, multiplier_1_cout;

  Multiplexer #(.width(32), .enable("false")) multiplexer_1 (
    .in0({32{1'b0}}), .in1(A), .out(multiplexer_1_out), .sel(B[31]));
  Multiplexer #(.width(32), .enable("false")) multiplexer_2 (
    .in0({32{1'b0}}), .in1(B), .out(multiplexer_2_out), .sel(A[31]));
  Adder #(.width(32)) adder_1 (.a(multiplexer_1_out), .b(multiplexer_2_out), .out(adder_1_out));  // open: cin, cout
  Multiplier #(.width(32)) multiplier_1 (.a(A), .b(B), .out(Lo), .cout(multiplier_1_cout));  // open: cin
  Adder #(.width(32)) adder_2 (.a(multiplier_1_cout), .b(adder_1_out), .out(Hi));  // open: cin, cout
endmodule

module Div (
  input  [31:0] A,
  input  [31:0] B,
  output [31:0] Lo,
  output [31:0] Hi
);

  wire xor_1_out;
  wire [31:0] divider_1_out, multiplexer_1_out, multiplexer_2_out, negator_1_out, negator_2_out,
       negator_3_out;

  Negator #(.width(32)) negator_1 (.in(A), .out(negator_1_out));
  Negator #(.width(32)) negator_2 (.in(B), .out(negator_2_out));
  Multiplexer #(.width(32), .enable("false")) multiplexer_1 (
    .in0(A), .in1(negator_1_out), .out(multiplexer_1_out), .sel(A[31]));
  Multiplexer #(.width(32), .enable("false")) multiplexer_2 (
    .in0(B), .in1(negator_2_out), .out(multiplexer_2_out), .sel(B[31]));
  Divider #(.width(32)) divider_1 (
    .a(multiplexer_1_out), .b(multiplexer_2_out), .out(divider_1_out), .rem(Hi));  // open: upper
  xor xor_1 (xor_1_out, A[31], B[31]);
  Negator #(.width(32)) negator_3 (.in(divider_1_out), .out(negator_3_out));
  Multiplexer #(.width(32), .enable("false")) multiplexer_3 (
    .in0(divider_1_out), .in1(negator_3_out), .out(Lo), .sel(xor_1_out));
endmodule
